# Fritzing sketch Solar Charger (saved by Fritzing 0.9.10b)
stripboards: 1

parts:
  Lead_Acid_Bat = 12 battery [package=battery]  # not connected
  Mod1 = Solar Charge Controller [part_number="KLD Series Solar Charge Controller PWM" package=PWM-Model]  # not connected
  Solar_Panel = Solar Cell  # not connected
  toCharger = Camdenboss CTB0158-2 [part_number=CTB0158-2 package=THT]
  fromPannel = Camdenboss CTB0158-2 [part_number=CTB0158-2 package=THT]
  fromCharger = Camdenboss CTB0158-2 [part_number=CTB0158-2 package=THT]
  toLoad = Camdenboss CTB0158-2 [part_number=CTB0158-2 package=THT]
  7805 = Voltage Regulator - 5V [package="TO220 [THT]"]
  7805_2 = Voltage Regulator - 5V [package="TO220 [THT]"]
  Pannel = INA219 DC Current Monitor Module [part_number=GY-219]
  toBat = Camdenboss CTB0158-2 [part_number=CTB0158-2 package=THT]
  Charge = INA219 DC Current Monitor Module [part_number=GY-219]
  Load = INA219 DC Current Monitor Module [part_number=GY-219]
  MCU1 = Raspberry Pi Zero
  Bauteil3 = Adafruit ISO1540 [part_number="Adafruit #4903"]
  Bauteil4 = Adafruit ISO1540 [part_number="Adafruit #4903"]

nets:
  N1: toCharger.pin1, 7805_2.input_voltage, Pannel.Vin-
  N2: toCharger.pin2, fromPannel.pin2
  N3: fromPannel.pin1, Pannel.Vin+
  N4: fromCharger.pin1, Charge.Vin+
  N5: fromCharger.pin2, toLoad.pin2, toBat.pin2
  N6: toLoad.pin1, 7805.input_voltage, Load.Vin-
  GND: 7805.GND, Charge.GND, Load.GND, Bauteil3.GND2
  VCC: 7805.output_voltage, Charge.VCC, Load.VCC, Bauteil3.VCC2
  GND_2: 7805_2.GND, Pannel.GND, Bauteil4.GND2
  N7: 7805_2.output_voltage, Pannel.VCC, Bauteil4.VCC2
  N8: Pannel.SCL, Bauteil4.SCL2
  N9: Pannel.SDA, Bauteil4.SDA2
  N10: toBat.pin1, Charge.Vin-, Load.Vin+
  N11: Charge.SCL, Load.SCL, Bauteil3.SCL2
  N12: Charge.SDA, Load.SDA, Bauteil3.SDA2
  N13: MCU1.pin_2, Bauteil3.VCC1, Bauteil4.VCC1
  N14: MCU1.pin_3, Bauteil3.SDA1, Bauteil4.SDA1
  N15: MCU1.pin_5, Bauteil3.SCL1, Bauteil4.SCL1
  GND1: MCU1.pin_6, Bauteil3.GND1, Bauteil4.GND1

notes:
  + Charger Pnl
  - Panel
  + Panel
  - Charger Pnl
  - Charger Bat
  + Charger Bat
  - Bat
  + Bat
  - Load
  + Load
  capacitors omitted
  SDA2
  SCL2
  Vreg Vin
  Vreg GND
  Vreg 5V
  SDA3
  SCL3
  SDA1
  SCL1
  GND
  Vi2c
  0
  1
  10
  5
  15
  20
  25
  30
  35

custom parts:
  12 battery: 12V lead acid type battery, like the Husqvarna YTH2448 12V 35AH battery. This is the mini version 1/4 the size of the actual battery to be closer to typical breadboard parts (around 2in wide rathher than 7in). The pads in pcb are sized to accomidate up to 14ga wire (as these batterys will deliver high currents.)
  Solar Charge Controller: PWM-Solar Charge Controller
  INA219 DC Current Monitor Module: INA219 DC Current Monitor Module Links: INA219 product information
  Adafruit ISO1540: Sometimes you'll find yourself with an I2C bus controller on one side, and an I2C bus device on the other and you gotta keep em (electrically) separated. Maybe because one is Earth-grounded, maybe because you've got some funky power monitoring setup, maybe you want to reduce noise. Whatever it is, you can use the Adafruit ISO1540 Bidirectional I2C Isolator to add full electrical isolation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
